// Logisim project Assignment2.1.circ as structural Verilog: 1 circuit, main circuit main
module main (
  input  A0,
  input  in_2,
  input  A1,
  input  [1:0] in_4,
  input  A2,
  input  A3,
  output MUX_out,
  output out_8
);

  wire multiplexer_2_out, multiplexer_3_out, multiplexer_4_out;

  Multiplexer #(.select(2)) multiplexer_1 (
    .in0(A0), .in1(A1), .in2(A2), .in3(A3), .out(MUX_out), .sel(in_4), .en(in_2));
  Multiplexer #(.enable("false")) multiplexer_2 (.in0(A0), .in1(A1), .out(multiplexer_2_out), .sel(in_4[0]));
  Multiplexer #(.enable("false")) multiplexer_3 (.in0(A2), .in1(A3), .out(multiplexer_3_out), .sel(in_4[0]));
  Multiplexer #(.enable("false")) multiplexer_4 (
    .in0(multiplexer_2_out), .in1(multiplexer_3_out), .out(multiplexer_4_out), .sel(in_4[1]));
  xor xor_1 (out_8, MUX_out, multiplexer_4_out);
endmodule
