// Logisim project Assignment3.1.circ as structural Verilog: 1 circuit, main circuit main
module main (
  input  Cin,
  input  [3:0] A,
  input  [3:0] B,
  output [3:0] out_4,
  output Cout
);

  Adder #(.width(4)) adder_1 (.a(A), .b(B), .out(out_4), .cin(Cin), .cout(Cout));
endmodule
