// Logisim project assignment4.2.circ as structural Verilog: 5 circuits, main circuit main
module main (
  input  CLK,
  input  D,
  output Q,
  output Q_prime
);

  wire and_1_out, and_2_out, not_1_out;

  not not_1 (not_1_out, D);
  and and_1 (and_1_out, CLK, not_1_out);
  and and_2 (and_2_out, CLK, D);
  nor nor_1 (Q, and_1_out, Q_prime);
  nor nor_2 (Q_prime, Q, and_2_out);
endmodule

module D_Flip_Flop (
  input  CLK,
  input  D,
  output Q
);

  wire main_1_q, not_1_out;

  not not_1 (not_1_out, CLK);
  main main_1 (.CLK(not_1_out), .D(D), .Q(main_1_q));  // open: Q_prime
  main main_2 (.CLK(CLK), .D(main_1_q), .Q(Q));  // open: Q_prime
endmodule

module _4_bit_register (
  input  CLK,
  input  [3:0] X,
  output [3:0] Y
);

  D_Flip_Flop d_ff_1 (.CLK(CLK), .D(X[0]), .Q(Y[0]));
  D_Flip_Flop d_ff_2 (.CLK(CLK), .D(X[1]), .Q(Y[1]));
  D_Flip_Flop d_ff_3 (.CLK(CLK), .D(X[2]), .Q(Y[2]));
  D_Flip_Flop d_ff_4 (.CLK(CLK), .D(X[3]), .Q(Y[3]));
endmodule

module SR_latch (
  input  R,
  input  S,
  output Q,
  output Q_prime
);

  nor nor_1 (Q, R, Q_prime);
  nor nor_2 (Q_prime, Q, S);
endmodule

module Sync_Seq_Circuit (
  input  [7:0] I,
  output [7:0] O
);

  wire button_1_out, clock_1_out;
  wire [7:0] multiplexer_1_out, not_1_out, register_1_q;

  Clock clock_1 (.out(clock_1_out));
  assign not_1_out = ~I;  // NOT_Gate not_1, 8 bits wide
  Register register_1 (.D(O), .Q(register_1_q), .clk(clock_1_out));  // open: en, clr
  Button button_1 (.out(button_1_out));
  Multiplexer #(.width(8), .enable("false")) multiplexer_1 (
    .in0(I), .in1(not_1_out), .out(multiplexer_1_out), .sel(button_1_out));
  Adder adder_1 (.a(register_1_q), .b(multiplexer_1_out), .out(O), .cin(button_1_out));  // open: cout
endmodule
